// Logisim project lab3_part_a.circ as structural Verilog: 3 circuits, main circuit main
module main (
);

  wire AB_sw1, AB_sw2, Clk_out, outputlogic_1_l, outputlogic_1_r, Reset_out;

  DipSwitch #(.number(2)) AB (.sw1(AB_sw1), .sw2(AB_sw2));
  Button Reset (.out(Reset_out));
  Button Clk (.out(Clk_out));
  outputlogic outputlogic_1 (
    .B(AB_sw2), .A(AB_sw1), .Clk(Clk_out), .Reset(Reset_out), .R(outputlogic_1_r), .L(outputlogic_1_l));
  LED led_1 (.in(outputlogic_1_r));
  LED led_2 (.in(outputlogic_1_l));
endmodule

module statelogic (
  input  B,
  input  A,
  input  Clk,
  input  Reset,
  output State1,
  output State0
);

  wire and_1_out, and_2_out, and_3_out, and_4_out, and_5_out, not_1_out, not_2_out, not_3_out, not_4_out,
       not_5_out, not_6_out, not_7_out, not_8_out, or_1_out, or_2_out;

  not not_1 (not_1_out, State1);
  not not_2 (not_2_out, State0);
  not not_3 (not_3_out, B);
  not not_4 (not_4_out, A);
  not not_5 (not_5_out, B);
  not not_6 (not_6_out, State1);
  not not_7 (not_7_out, State0);
  not not_8 (not_8_out, A);
  and and_1 (and_1_out, not_1_out, State0, B);
  and and_2 (and_2_out, State1, not_2_out);
  and and_3 (and_3_out, State1, not_3_out, not_4_out);
  and and_4 (and_4_out, not_6_out, not_7_out, A);
  and and_5 (and_5_out, State1, not_7_out, not_8_out);
  D_Flip_Flop Q1 (.D(or_1_out), .clk(Clk), .Q(State1), .reset(Reset));  // open: Qn, preset
  or or_1 (or_1_out, and_1_out, and_2_out, and_3_out);
  D_Flip_Flop Q0 (.D(or_2_out), .clk(Clk), .Q(State0), .reset(Reset));  // open: Qn, preset
  or or_2 (or_2_out, not_5_out, and_4_out, and_5_out);
endmodule

module outputlogic (
  input  B,
  input  A,
  input  Clk,
  input  Reset,
  output R,
  output L
);

  wire and_1_out, and_2_out, and_3_out, and_4_out, and_5_out, not_1_out, not_2_out, not_3_out, not_4_out,
       statelogic_1_state0, statelogic_1_state1;

  statelogic statelogic_1 (
    .B(B), .A(A), .Clk(Clk), .Reset(Reset), .State1(statelogic_1_state1), .State0(statelogic_1_state0));
  not not_1 (not_1_out, statelogic_1_state1);
  not not_2 (not_2_out, statelogic_1_state0);
  not not_3 (not_3_out, B);
  not not_4 (not_4_out, A);
  and and_1 (and_1_out, not_1_out, not_2_out, A);
  and and_2 (and_2_out, not_1_out, not_3_out);
  and and_3 (and_3_out, not_3_out, A);
  and and_4 (and_4_out, statelogic_1_state1, not_2_out, not_4_out);
  and and_5 (and_5_out, statelogic_1_state1, not_3_out, not_4_out);
  or or_1 (R, and_1_out, and_2_out, and_3_out);
  or or_2 (L, and_4_out, and_5_out);
endmodule
