// Logisim project lab04_base.circ as structural Verilog: 4 circuits, main circuit register_file
module register_file (
  input  [7:0] data_write,
  input  [1:0] write_reg,
  input  clear,
  input  write_enable,
  input  [1:0] read_reg,
  input  clk,
  input  reset,
  output [7:0] data_read
);

  wire demultiplexer_2_out0, demultiplexer_2_out1, demultiplexer_2_out2, demultiplexer_2_out3;
  wire [7:0] demultiplexer_1_out0, demultiplexer_1_out1, demultiplexer_1_out2, demultiplexer_1_out3,
       multiplexer_1_out, multiplexer_2_out, multiplexer_3_out, multiplexer_4_out, R0_q, R1_q, R2_q, R3_q;

  Demultiplexer #(.select(2), .width(8)) demultiplexer_1 (
    .out0(demultiplexer_1_out0), .out1(demultiplexer_1_out1), .out2(demultiplexer_1_out2),
    .out3(demultiplexer_1_out3), .in(data_write), .sel(write_reg));
  Multiplexer #(.width(8)) multiplexer_1 (
    .in0(demultiplexer_1_out0), .in1({8{1'b0}}), .out(multiplexer_1_out), .sel(clear));
  Multiplexer #(.width(8)) multiplexer_2 (
    .in0(demultiplexer_1_out1), .in1({8{1'b0}}), .out(multiplexer_2_out), .sel(clear));
  Demultiplexer #(.select(2)) demultiplexer_2 (
    .out0(demultiplexer_2_out0), .out1(demultiplexer_2_out1), .out2(demultiplexer_2_out2),
    .out3(demultiplexer_2_out3), .in(write_enable), .sel(write_reg));
  Multiplexer #(.width(8)) multiplexer_3 (
    .in0(demultiplexer_1_out2), .in1({8{1'b0}}), .out(multiplexer_3_out), .sel(clear));
  Multiplexer #(.width(8)) multiplexer_4 (
    .in0(demultiplexer_1_out3), .in1({8{1'b0}}), .out(multiplexer_4_out), .sel(clear));
  Register R0 (.D(multiplexer_1_out), .en(demultiplexer_2_out0), .clk(clk), .Q(R0_q), .clr(reset));
  Register R1 (.D(multiplexer_2_out), .en(demultiplexer_2_out1), .clk(clk), .Q(R1_q), .clr(reset));
  Register R2 (.D(multiplexer_3_out), .en(demultiplexer_2_out2), .clk(clk), .Q(R2_q), .clr(reset));
  Register R3 (.D(multiplexer_4_out), .en(demultiplexer_2_out3), .clk(clk), .Q(R3_q), .clr(reset));
  Multiplexer #(.select(2), .width(8)) multiplexer_5 (
    .in0(R0_q), .in1(R1_q), .in2(R2_q), .in3(R3_q), .out(data_read), .sel(read_reg));
endmodule

module alu (
  input  [7:0] A,
  input  [7:0] B,
  input  op,
  output [7:0] data_out
);

  wire [7:0] adder_1_out, multiplier_1_out;

  Multiplier multiplier_1 (.a(A), .b(B), .out(multiplier_1_out));  // open: cin, cout
  Adder adder_1 (.a(A), .b(B), .out(adder_1_out));  // open: cin, cout
  Multiplexer #(.width(8)) multiplexer_1 (.in0(multiplier_1_out), .in1(adder_1_out), .out(data_out), .sel(op));
endmodule

module instr_decoder (
  input  [7:0] instr,
  output [1:0] imm,
  output [1:0] read_reg,
  output [1:0] write_reg,
  output alu_op,
  output write_en,
  output reg_clear
);

  not not_1 (alu_op, instr[6]);
  or or_1 (write_en, instr[6], instr[7]);
  and and_1 (reg_clear, instr[7], instr[6]);

  assign imm = instr[1:0];
  assign read_reg = instr[3:2];
  assign write_reg = instr[5:4];
endmodule

module main (
  input  [7:0] in_1
);

  wire Clk_out, instr_decoder_1_alu_op, instr_decoder_1_reg_clear, instr_decoder_1_write_en, Reset_out;
  wire [1:0] instr_decoder_1_imm, instr_decoder_1_read_reg, instr_decoder_1_write_reg;
  wire [7:0] alu_1_data_out, bit_extender_1_out, register_file_1_data_read;

  Button Reset (.out(Reset_out));
  Button Clk (.out(Clk_out));
  instr_decoder instr_decoder_1 (
    .instr(in_1), .imm(instr_decoder_1_imm), .read_reg(instr_decoder_1_read_reg),
    .write_reg(instr_decoder_1_write_reg), .alu_op(instr_decoder_1_alu_op),
    .write_en(instr_decoder_1_write_en), .reg_clear(instr_decoder_1_reg_clear));
  assign bit_extender_1_out = {{6{1'b0}}, instr_decoder_1_imm};  // Bit_Extender bit_extender_1
  register_file register_file_1 (
    .data_write(alu_1_data_out), .write_reg(instr_decoder_1_write_reg), .clear(instr_decoder_1_reg_clear),
    .write_enable(instr_decoder_1_write_en), .read_reg(instr_decoder_1_read_reg), .clk(Clk_out),
    .reset(Reset_out), .data_read(register_file_1_data_read));
  alu alu_1 (
    .A(register_file_1_data_read), .B(bit_extender_1_out), .op(instr_decoder_1_alu_op),
    .data_out(alu_1_data_out));
endmodule
